# Fritzing sketch incubadora (saved by Fritzing 0.9.6b)
breadboards: 1

parts:
  KY-2 = Keyes Relay [package=THT]
  Part3 = Lilypad Battery Connect  # not connected
  U1 = LCD-16X2 [package=lcd-16x2]
  Driver3 = 28BYJ-48 Driver Module [part_number=ULN2003 package=THT]  # not connected
  Componente1 = Arduino Leonardo (Rev3b)
  LCM1602_IIC1 = LCM1602 IIC [part_number="LCM1602 IIC" chip_label="LCM1602 IIC" package="DIP (Dual Inline) [THT]"]
  YF-S201_Flow_Meter2 = YF-S201 Water Flow Meter
  M1 = E18-D80NK_1 [package=THT]
  VALVE1 = Plastic Solenoid Valve
  VCC1 = Battery block 9V
  Parte3 = SRF05 Ultrasonic Rangefinder
  LED4 = smd LED [color="Green (555nm)" package="0805 [SMD]"]
  R4 = Resistor [tolerance=±5% resistance=220 package="1206 [SMD]"]
  LED5 = smd LED [color="Blue (525nm)" package="0805 [SMD]"]
  R5 = Resistor [tolerance=±5% resistance=220 package="1206 [SMD]"]
  LED6 = smd LED [color="Yellow (595nm)" package="0805 [SMD]"]
  R6 = Resistor [tolerance=±5% resistance=220 package="1206 [SMD]"]

nets:
  N1: KY-2.signal, Componente1.D13_PWM
  VCC: KY-2.power, Componente1.5V, LCM1602_IIC1.VCC, YF-S201_Flow_Meter2.VCC, M1.pin2, Parte3.VCC, R4.Pin_1, R5.Pin_1, R6.Pin_1
  GND: KY-2.ground, Componente1.GND, LCM1602_IIC1.GND, YF-S201_Flow_Meter2.GND, M1.pin1, Parte3.GND
  N2: KY-2.NC, VALVE1.no_name_yet
  N3: KY-2.C, VCC1.-
  VSS: U1.VSS, LCM1602_IIC1.VSS
  VDD: U1.VDD, LCM1602_IIC1.VDD
  N4: U1.VO, LCM1602_IIC1.V0
  N5: U1.RS, LCM1602_IIC1.RS
  N6: U1.R_W, LCM1602_IIC1.RW
  N7: U1.E, LCM1602_IIC1.E
  N8: U1.DB0, LCM1602_IIC1.D0
  N9: U1.DB1, LCM1602_IIC1.D1
  N10: U1.DB2, LCM1602_IIC1.D2
  N11: U1.DB3, LCM1602_IIC1.D3
  N12: U1.DB4, LCM1602_IIC1.D4
  N13: U1.DB5, LCM1602_IIC1.D5
  N14: U1.DB6, LCM1602_IIC1.D6
  N15: U1.DB7, LCM1602_IIC1.D7
  N16: U1.A, LCM1602_IIC1.A
  N17: U1.K, LCM1602_IIC1.K
  N18: Componente1.D2/SDA, Componente1.SDA, LCM1602_IIC1.SDA, LED4.cathode
  N19: Componente1.D3_PWM/SCL, Componente1.SCL, LCM1602_IIC1.SCL, LED5.cathode
  N20: Componente1.D4/A6, LED6.cathode
  N21: Componente1.D6_PWM/A7, M1.pin3
  N22: Componente1.D7, YF-S201_Flow_Meter2.SIG
  N23: Componente1.D9_PWM/A9, Parte3.Trig
  N24: Componente1.D10_PWM/A10, Parte3.Echo
  N25: LCM1602_IIC1.LED_A, LCM1602_IIC1.LED_B
  N26: LED4.anode, R4.Pin_0
  N27: LED5.anode, R5.Pin_0
  N28: LED6.anode, R6.Pin_0

custom parts:
  Keyes Relay: The Keyes 5V relay module is suitable for SCM development, home appliance control. It uses a 5V~12V TIL control signal which can control DC / AC signal.
  28BYJ-48 Driver Module: Generic male header
  LCM1602 IIC: I2C-Module to use a 1602 or 2004 LCD on with the wire.h libory Serial LCD Modul
  YF-S201 Water Flow Meter: The YF-S201 Flow Meter. The input voltage is 5V to 24V (DC).
  E18-D80NK_1: E18-D80NK Proximity Sensor module.

// code stored in the sketch: Untitled.ino
#include <Stepper.h>
#include <Wire.h>
#include <LiquidCrystal_I2C.h>
#include "DHT.h"

#define DHTPIN 12
#define DHTTYPE DHT11 // DHT22

LiquidCrystal_I2C lcd(0x27, 16, 2);

// Configuración de los pasos del motor
const int stepsPerRevolution = 2048; // Pasos por revolución (28BYJ-48)

DHT dht(DHTPIN, DHTTYPE);
int vcc = 11; // Pin de alimentación

// Pines de conexión al módulo ULN2003
const int IN1 = 7;
const int IN2 = 6;
const int IN3 = 5;
const int IN4 = 4;

// Crear objeto Stepper
Stepper myStepper(stepsPerRevolution, IN1, IN3, IN2, IN4);

// Variable para rastrear la posición actual del motor
int posicionActual = 0;

// Variables para el tiempo
unsigned long tiempoInicio = 0;
unsigned long tiempoTranscurrido = 0;

void mesajeInicio(){
  lcd.clear(); // Limpia el LCD
  lcd.setCursor(2, 0);
  lcd.print("Iniciando");
  lcd.setCursor(2, 1);
  lcd.print("Incubadora");
  lcd.setCursor(14, 0);  // Posición de la columna 10, fila 1
  lcd.write(0);          // Imprimir el primer carácter personalizado
  lcd.write(1);          // Imprimir el segundo carácter personalizado
  lcd.setCursor(14, 1);  // Posición de la columna 10, fila 1
  lcd.write(2);          // Imprimir el tercer carácter personalizado
  lcd.write(3);          // Imprimir el cuarto carácter personalizado
  delay(8000);  // Esperar
}

void setup() {
  lcd.init();
  lcd.backlight();
  lcd.clear();

  pinMode(vcc, OUTPUT);
  dht.begin();

  // Crear caracteres personalizados
  uint8_t char0[] = {0x1F, 0x10, 0x10, 0x10, 0x10, 0x17, 0x14, 0x14};  // Ejemplo de carácter
  uint8_t char1[] = {0x1F, 0x07, 0x07, 0x07, 0x07, 0x1F, 0x03, 0x03};  // Ejemplo de carácter
  uint8_t char2[] = {0x1C, 0x1C, 0x1E, 0x1F, 0x1F, 0x1F, 0x00, 0x00};  // Ejemplo de carácter
  uint8_t char3[] = {0x03, 0x03, 0x07, 0x0F, 0x1F, 0x1F, 0x00, 0x00};  // Ejemplo de carácter
  
  lcd.createChar(0, char0);  // Crear el primer carácter
  lcd.createChar(1, char1);  // Crear el segundo carácter
  lcd.createChar(2, char2);  // Crear el tercer carácter
  lcd.createChar(3, char3);  // Crear el cuarto carácter

  // Configurar la velocidad del motor (en RPM)
  myStepper.setSpeed(15);
  Serial.begin(9600);
  Serial.println("Motor iniciado. Girando en un solo sentido...");

  // Registrar el tiempo de inicio
  tiempoInicio = millis(); // Almacena el tiempo en milisegundos desde que el programa comenzó
  posicionActual = 0;

  // Mostrar mensaje de inicio
  mesajeInicio();  // Muestra el mensaje de inicio
}

void loop() {
  digitalWrite(vcc, HIGH);

  // Calcular el tiempo transcurrido
  tiempoTranscurrido = millis() - tiempoInicio;

  // Convertir tiempo transcurrido a horas, minutos y segundos
  unsigned long segundos = (tiempoTranscurrido / 1000) % 60;
  unsigned long minutos = (tiempoTranscurrido / 1000 / 60) % 60;
  unsigned long horas = (tiempoTranscurrido / 1000 / 60 / 60);

  int t = dht.readTemperature(); // Lee la temperatura

  lcd.clear(); // Limpia el LCD
  lcd.setCursor(0, 0);
  lcd.print("Time: ");
  lcd.print(horas);
  lcd.print("h ");
  lcd.print(minutos);
  lcd.print("m ");
  lcd.print(segundos);
  lcd.print("s");

  lcd.setCursor(0, 1);
  lcd.print("Temp: ");
  lcd.print(t);
  lcd.print("C");
  delay(500);

  if (t > 35) {
 
    lcd.clear();
    lcd.setCursor(2, 0);
    lcd.print("Estabilizar ");
    lcd.setCursor(2, 1);
    lcd.print("Temperatura ");
    delay(1000); // Pausa para mostrar mensaje

    // Regresar a la posición inicial
    Serial.println("Temperatura alta, regresando a posición inicial...");
    myStepper.step(-posicionActual); // Pasos en dirección opuesta
    posicionActual = 0;             // Resetear la posición actual

  } else {
    // Girar el motor hacia adelante
    Serial.println("Motor girando...");
    myStepper.step(100); // Mueve 100 pasos hacia adelante
    posicionActual += 100; // Actualiza la posición actual


  }
}
